// Logisim project control-logic.circ as structural Verilog: 1 circuit, main circuit control_logic
module control_logic (
  input  [31:0] Instruction,
  input  BrEq,
  input  BrLt,
  output PCSel,
  output RegWEn,
  output [2:0] ImmSel,
  output BrUn,
  output ASel,
  output BSel,
  output [3:0] ALUSel,
  output MemWEn,
  output [1:0] WBSel
);

  wire and_5_out, and_6_out, and_7_out, and_10_out, and_11_out, and_12_out, and_13_out, and_14_out,
       and_15_out, and_16_out, and_17_out, and_18_out, and_19_out, and_20_out, and_21_out, and_49_out,
       and_50_out, and_52_out, and_53_out, comparator_1_eq, comparator_2_eq, comparator_3_eq,
       comparator_4_eq, comparator_5_eq, comparator_6_eq, comparator_7_eq, comparator_8_eq, comparator_9_eq,
       comparator_10_eq, comparator_11_eq, comparator_12_eq, comparator_13_eq, comparator_14_eq,
       comparator_15_eq, comparator_16_eq, comparator_17_eq, comparator_18_eq, comparator_19_eq,
       comparator_20_eq, comparator_21_eq, comparator_22_eq, comparator_23_eq, comparator_24_eq,
       comparator_25_eq, comparator_26_eq, comparator_27_eq, comparator_28_eq, comparator_29_eq,
       comparator_30_eq, comparator_31_eq, comparator_32_eq, comparator_33_eq, comparator_34_eq,
       comparator_35_eq, comparator_36_eq, comparator_37_eq, comparator_38_eq, comparator_39_eq,
       comparator_40_eq, comparator_41_eq, comparator_42_eq, comparator_43_eq, comparator_44_eq,
       comparator_45_eq, comparator_46_eq, comparator_47_eq, comparator_48_eq, comparator_49_eq,
       comparator_50_eq, comparator_51_eq, comparator_52_eq, comparator_53_eq, comparator_54_eq,
       comparator_55_eq, comparator_56_eq, comparator_57_eq, comparator_58_eq, comparator_59_eq,
       comparator_60_eq, comparator_61_eq, comparator_62_eq, comparator_63_eq, comparator_64_eq,
       comparator_65_eq, comparator_66_eq, comparator_67_eq, comparator_68_eq, comparator_69_eq,
       comparator_70_eq, comparator_71_eq, comparator_72_eq, comparator_73_eq, comparator_74_eq,
       comparator_75_eq, comparator_76_eq, comparator_77_eq, comparator_78_eq, comparator_79_eq,
       comparator_80_eq, comparator_81_eq, comparator_83_eq, comparator_84_eq, IsAdd, IsAddi, IsAnd, IsAndi,
       IsAuipc, IsBeq, IsBge, IsBgeu, IsBlt, IsBltu, IsBne, IsJal, IsJalr, IsLb, IsLh, IsLui, IsLw, IsMul,
       IsMulh, IsMulhu, IsOr, IsOri, IsSb, IsSh, IsSll, IsSlli, IsSlt, IsSlti, IsSltiu, IsSra, IsSrai, IsSrl,
       IsSrli, IsSub, IsSw, IsXor, IsXori, or_1_out, or_2_out, or_3_out, or_5_out, undriven, undriven_2,
       undriven_3, undriven_4, undriven_5, undriven_6, undriven_7, undriven_8, undriven_9, undriven_10,
       undriven_11, undriven_12, undriven_13, undriven_14, undriven_15, undriven_16, undriven_17,
       undriven_18, undriven_19, undriven_20, undriven_21, undriven_22, undriven_23, undriven_24,
       undriven_25, undriven_26, undriven_27, undriven_28;
  wire [5:0] ROMIn;
  wire [15:14] rom_1_data;

  // Probe on Instruction[6:0]
  Comparator #(.mode("unsigned"), .width(7)) comparator_1 (
    .a(Instruction[6:0]), .b(7'b0010011), .eq(comparator_1_eq));  // open: gt, lt
  Comparator #(.mode("unsigned"), .width(3)) comparator_2 (
    .a(Instruction[14:12]), .b(3'b000), .eq(comparator_2_eq));  // open: gt, lt
  Comparator #(.mode("unsigned"), .width(7)) comparator_3 (
    .a(Instruction[6:0]), .b(7'b0010011), .eq(comparator_3_eq));  // open: gt, lt
  Comparator #(.mode("unsigned"), .width(3)) comparator_4 (
    .a(Instruction[14:12]), .b(3'b111), .eq(comparator_4_eq));  // open: gt, lt
  Comparator #(.mode("unsigned"), .width(7)) comparator_5 (
    .a(Instruction[6:0]), .b(7'b0010011), .eq(comparator_5_eq));  // open: gt, lt
  Comparator #(.mode("unsigned"), .width(3)) comparator_6 (
    .a(Instruction[14:12]), .b(3'b110), .eq(comparator_6_eq));  // open: gt, lt
  Comparator #(.mode("unsigned"), .width(7)) comparator_7 (
    .a(Instruction[6:0]), .b(7'b0010011), .eq(comparator_7_eq));  // open: gt, lt
  Comparator #(.mode("unsigned"), .width(3)) comparator_8 (
    .a(Instruction[14:12]), .b(3'b100), .eq(comparator_8_eq));  // open: gt, lt
  Comparator #(.mode("unsigned"), .width(7)) comparator_9 (
    .a(Instruction[6:0]), .b(7'b0010011), .eq(comparator_9_eq));  // open: gt, lt
  Comparator #(.mode("unsigned"), .width(3)) comparator_10 (
    .a(Instruction[14:12]), .b(3'b001), .eq(comparator_10_eq));  // open: gt, lt
  Comparator #(.mode("unsigned"), .width(7)) comparator_11 (
    .a(Instruction[31:25]), .b({7{1'b0}}), .eq(comparator_11_eq));  // open: gt, lt
  Comparator #(.mode("unsigned"), .width(7)) comparator_12 (
    .a(Instruction[6:0]), .b(7'b0010011), .eq(comparator_12_eq));  // open: gt, lt
  Comparator #(.mode("unsigned"), .width(3)) comparator_13 (
    .a(Instruction[14:12]), .b(3'b101), .eq(comparator_13_eq));  // open: gt, lt
  Comparator #(.mode("unsigned"), .width(7)) comparator_14 (
    .a(Instruction[31:25]), .b({7{1'b0}}), .eq(comparator_14_eq));  // open: gt, lt
  Comparator #(.mode("unsigned"), .width(7)) comparator_15 (
    .a(Instruction[6:0]), .b(7'b0010011), .eq(comparator_15_eq));  // open: gt, lt
  Comparator #(.mode("unsigned"), .width(3)) comparator_16 (
    .a(Instruction[14:12]), .b(3'b101), .eq(comparator_16_eq));  // open: gt, lt
  Comparator #(.mode("unsigned"), .width(7)) comparator_17 (
    .a(Instruction[31:25]), .b(7'b0100000), .eq(comparator_17_eq));  // open: gt, lt
  Comparator #(.mode("unsigned"), .width(7)) comparator_18 (
    .a(Instruction[6:0]), .b(7'b0010011), .eq(comparator_18_eq));  // open: gt, lt
  Comparator #(.mode("unsigned"), .width(3)) comparator_19 (
    .a(Instruction[14:12]), .b(3'b010), .eq(comparator_19_eq));  // open: gt, lt
  Comparator #(.mode("unsigned"), .width(7)) comparator_20 (
    .a(Instruction[6:0]), .b(7'b0010011), .eq(comparator_20_eq));  // open: gt, lt
  Comparator #(.mode("unsigned"), .width(3)) comparator_21 (
    .a(Instruction[14:12]), .b(3'b011), .eq(comparator_21_eq));  // open: gt, lt
  Comparator #(.mode("unsigned"), .width(7)) comparator_22 (
    .a(Instruction[6:0]), .b(7'b0110011), .eq(comparator_22_eq));  // open: gt, lt
  Comparator #(.mode("unsigned"), .width(3)) comparator_23 (
    .a(Instruction[14:12]), .b(3'b000), .eq(comparator_23_eq));  // open: gt, lt
  Comparator #(.mode("unsigned"), .width(7)) comparator_24 (
    .a(Instruction[31:25]), .b({7{1'b0}}), .eq(comparator_24_eq));  // open: gt, lt
  Comparator #(.mode("unsigned"), .width(7)) comparator_25 (
    .a(Instruction[6:0]), .b(7'b0110011), .eq(comparator_25_eq));  // open: gt, lt
  Comparator #(.mode("unsigned"), .width(3)) comparator_26 (
    .a(Instruction[14:12]), .b(3'b000), .eq(comparator_26_eq));  // open: gt, lt
  Comparator #(.mode("unsigned"), .width(7)) comparator_27 (
    .a(Instruction[31:25]), .b(7'b0100000), .eq(comparator_27_eq));  // open: gt, lt
  Comparator #(.mode("unsigned"), .width(7)) comparator_28 (
    .a(Instruction[6:0]), .b(7'b0110011), .eq(comparator_28_eq));  // open: gt, lt
  Comparator #(.mode("unsigned"), .width(3)) comparator_29 (
    .a(Instruction[14:12]), .b(3'b111), .eq(comparator_29_eq));  // open: gt, lt
  Comparator #(.mode("unsigned"), .width(7)) comparator_30 (
    .a(Instruction[31:25]), .b({7{1'b0}}), .eq(comparator_30_eq));  // open: gt, lt
  Comparator #(.mode("unsigned"), .width(7)) comparator_31 (
    .a(Instruction[6:0]), .b(7'b0110011), .eq(comparator_31_eq));  // open: gt, lt
  Comparator #(.mode("unsigned"), .width(3)) comparator_32 (
    .a(Instruction[14:12]), .b(3'b110), .eq(comparator_32_eq));  // open: gt, lt
  Comparator #(.mode("unsigned"), .width(7)) comparator_33 (
    .a(Instruction[31:25]), .b({7{1'b0}}), .eq(comparator_33_eq));  // open: gt, lt
  Comparator #(.mode("unsigned"), .width(7)) comparator_34 (
    .a(Instruction[6:0]), .b(7'b0110011), .eq(comparator_34_eq));  // open: gt, lt
  Comparator #(.mode("unsigned"), .width(3)) comparator_35 (
    .a(Instruction[14:12]), .b(3'b100), .eq(comparator_35_eq));  // open: gt, lt
  Comparator #(.mode("unsigned"), .width(7)) comparator_36 (
    .a(Instruction[31:25]), .b({7{1'b0}}), .eq(comparator_36_eq));  // open: gt, lt
  Comparator #(.mode("unsigned"), .width(7)) comparator_37 (
    .a(Instruction[6:0]), .b(7'b0110011), .eq(comparator_37_eq));  // open: gt, lt
  Comparator #(.mode("unsigned"), .width(3)) comparator_38 (
    .a(Instruction[14:12]), .b(3'b001), .eq(comparator_38_eq));  // open: gt, lt
  Comparator #(.mode("unsigned"), .width(7)) comparator_39 (
    .a(Instruction[31:25]), .b({7{1'b0}}), .eq(comparator_39_eq));  // open: gt, lt
  Comparator #(.mode("unsigned"), .width(7)) comparator_40 (
    .a(Instruction[6:0]), .b(7'b0110011), .eq(comparator_40_eq));  // open: gt, lt
  Comparator #(.mode("unsigned"), .width(3)) comparator_41 (
    .a(Instruction[14:12]), .b(3'b101), .eq(comparator_41_eq));  // open: gt, lt
  Comparator #(.mode("unsigned"), .width(7)) comparator_42 (
    .a(Instruction[31:25]), .b({7{1'b0}}), .eq(comparator_42_eq));  // open: gt, lt
  Comparator #(.mode("unsigned"), .width(7)) comparator_43 (
    .a(Instruction[6:0]), .b(7'b0110011), .eq(comparator_43_eq));  // open: gt, lt
  Comparator #(.mode("unsigned"), .width(3)) comparator_44 (
    .a(Instruction[14:12]), .b(3'b101), .eq(comparator_44_eq));  // open: gt, lt
  Comparator #(.mode("unsigned"), .width(7)) comparator_45 (
    .a(Instruction[31:25]), .b(7'b0100000), .eq(comparator_45_eq));  // open: gt, lt
  Comparator #(.mode("unsigned"), .width(7)) comparator_46 (
    .a(Instruction[6:0]), .b(7'b0110011), .eq(comparator_46_eq));  // open: gt, lt
  Comparator #(.mode("unsigned"), .width(3)) comparator_47 (
    .a(Instruction[14:12]), .b(3'b010), .eq(comparator_47_eq));  // open: gt, lt
  Comparator #(.mode("unsigned"), .width(7)) comparator_48 (
    .a(Instruction[31:25]), .b({7{1'b0}}), .eq(comparator_48_eq));  // open: gt, lt
  Comparator #(.mode("unsigned"), .width(7)) comparator_49 (
    .a(Instruction[6:0]), .b(7'b0110011), .eq(comparator_49_eq));  // open: gt, lt
  Comparator #(.mode("unsigned"), .width(3)) comparator_50 (
    .a(Instruction[14:12]), .b(3'b000), .eq(comparator_50_eq));  // open: gt, lt
  Comparator #(.mode("unsigned"), .width(7)) comparator_51 (
    .a(Instruction[31:25]), .b(7'b0000001), .eq(comparator_51_eq));  // open: gt, lt
  Comparator #(.mode("unsigned"), .width(7)) comparator_52 (
    .a(Instruction[6:0]), .b(7'b0110011), .eq(comparator_52_eq));  // open: gt, lt
  Comparator #(.mode("unsigned"), .width(3)) comparator_53 (
    .a(Instruction[14:12]), .b(3'b001), .eq(comparator_53_eq));  // open: gt, lt
  Comparator #(.mode("unsigned"), .width(7)) comparator_54 (
    .a(Instruction[31:25]), .b(7'b0000001), .eq(comparator_54_eq));  // open: gt, lt
  Comparator #(.mode("unsigned"), .width(7)) comparator_55 (
    .a(Instruction[6:0]), .b(7'b0110011), .eq(comparator_55_eq));  // open: gt, lt
  Comparator #(.mode("unsigned"), .width(3)) comparator_56 (
    .a(Instruction[14:12]), .b(3'b011), .eq(comparator_56_eq));  // open: gt, lt
  Comparator #(.mode("unsigned"), .width(7)) comparator_57 (
    .a(Instruction[31:25]), .b(7'b0000001), .eq(comparator_57_eq));  // open: gt, lt
  // Probe on Instruction[14:12]
  and and_1 (IsAddi, comparator_1_eq, comparator_2_eq);
  and and_2 (IsAndi, comparator_3_eq, comparator_4_eq);
  and and_3 (IsOri, comparator_5_eq, comparator_6_eq);
  and and_4 (IsXori, comparator_7_eq, comparator_8_eq);
  and and_5 (and_5_out, comparator_9_eq, comparator_10_eq);
  and and_6 (and_6_out, comparator_12_eq, comparator_13_eq);
  and and_7 (and_7_out, comparator_15_eq, comparator_16_eq);
  and and_8 (IsSlti, comparator_18_eq, comparator_19_eq);
  and and_9 (IsSltiu, comparator_20_eq, comparator_21_eq);
  and and_10 (and_10_out, comparator_22_eq, comparator_23_eq);
  and and_11 (and_11_out, comparator_25_eq, comparator_26_eq);
  and and_12 (and_12_out, comparator_28_eq, comparator_29_eq);
  and and_13 (and_13_out, comparator_31_eq, comparator_32_eq);
  and and_14 (and_14_out, comparator_34_eq, comparator_35_eq);
  and and_15 (and_15_out, comparator_37_eq, comparator_38_eq);
  and and_16 (and_16_out, comparator_40_eq, comparator_41_eq);
  and and_17 (and_17_out, comparator_43_eq, comparator_44_eq);
  and and_18 (and_18_out, comparator_46_eq, comparator_47_eq);
  and and_19 (and_19_out, comparator_49_eq, comparator_50_eq);
  and and_20 (and_20_out, comparator_52_eq, comparator_53_eq);
  and and_21 (and_21_out, comparator_55_eq, comparator_56_eq);
  and and_22 (IsSlli, and_5_out, comparator_11_eq);
  and and_23 (IsSrli, and_6_out, comparator_14_eq);
  and and_24 (IsSrai, and_7_out, comparator_17_eq);
  and and_25 (IsAdd, and_10_out, comparator_24_eq);
  and and_26 (IsSub, and_11_out, comparator_27_eq);
  and and_27 (IsAnd, and_12_out, comparator_30_eq);
  and and_28 (IsOr, and_13_out, comparator_33_eq);
  and and_29 (IsXor, and_14_out, comparator_36_eq);
  and and_30 (IsSll, and_15_out, comparator_39_eq);
  and and_31 (IsSrl, and_16_out, comparator_42_eq);
  and and_32 (IsSra, and_17_out, comparator_45_eq);
  and and_33 (IsSlt, and_18_out, comparator_48_eq);
  and and_34 (IsMul, and_19_out, comparator_51_eq);
  and and_35 (IsMulh, and_20_out, comparator_54_eq);
  and and_36 (IsMulhu, and_21_out, comparator_57_eq);
  ROM #(.addrWidth(6), .dataWidth(16)) rom_1 (
    .addr(ROMIn), .data({rom_1_data, WBSel, MemWEn, ALUSel, BSel, ASel, BrUn, ImmSel, RegWEn}));
  Comparator #(.mode("unsigned"), .width(7)) comparator_58 (
    .a(Instruction[6:0]), .b(7'b1100011), .eq(comparator_58_eq));  // open: gt, lt
  Comparator #(.mode("unsigned"), .width(3)) comparator_59 (
    .a(Instruction[14:12]), .b(3'b000), .eq(comparator_59_eq));  // open: gt, lt
  Comparator #(.mode("unsigned"), .width(7)) comparator_60 (
    .a(Instruction[6:0]), .b(7'b1100011), .eq(comparator_60_eq));  // open: gt, lt
  Comparator #(.mode("unsigned"), .width(3)) comparator_61 (
    .a(Instruction[14:12]), .b(3'b101), .eq(comparator_61_eq));  // open: gt, lt
  Comparator #(.mode("unsigned"), .width(7)) comparator_62 (
    .a(Instruction[6:0]), .b(7'b1100011), .eq(comparator_62_eq));  // open: gt, lt
  Comparator #(.mode("unsigned"), .width(3)) comparator_63 (
    .a(Instruction[14:12]), .b(3'b111), .eq(comparator_63_eq));  // open: gt, lt
  Comparator #(.mode("unsigned"), .width(7)) comparator_64 (
    .a(Instruction[6:0]), .b(7'b1100011), .eq(comparator_64_eq));  // open: gt, lt
  Comparator #(.mode("unsigned"), .width(3)) comparator_65 (
    .a(Instruction[14:12]), .b(3'b100), .eq(comparator_65_eq));  // open: gt, lt
  Comparator #(.mode("unsigned"), .width(7)) comparator_66 (
    .a(Instruction[6:0]), .b(7'b1100011), .eq(comparator_66_eq));  // open: gt, lt
  Comparator #(.mode("unsigned"), .width(3)) comparator_67 (
    .a(Instruction[14:12]), .b(3'b110), .eq(comparator_67_eq));  // open: gt, lt
  Comparator #(.mode("unsigned"), .width(7)) comparator_68 (
    .a(Instruction[6:0]), .b(7'b1100011), .eq(comparator_68_eq));  // open: gt, lt
  Comparator #(.mode("unsigned"), .width(3)) comparator_69 (
    .a(Instruction[14:12]), .b(3'b001), .eq(comparator_69_eq));  // open: gt, lt
  and and_37 (IsBeq, comparator_58_eq, comparator_59_eq);
  and and_38 (IsBge, comparator_60_eq, comparator_61_eq);
  and and_39 (IsBgeu, comparator_62_eq, comparator_63_eq);
  and and_40 (IsBlt, comparator_64_eq, comparator_65_eq);
  and and_41 (IsBltu, comparator_66_eq, comparator_67_eq);
  and and_42 (IsBne, comparator_68_eq, comparator_69_eq);
  Comparator #(.mode("unsigned"), .width(7)) comparator_70 (
    .a(Instruction[6:0]), .b(7'b0000011), .eq(comparator_70_eq));  // open: gt, lt
  and and_43 (IsLb, comparator_70_eq, comparator_71_eq);
  Comparator #(.mode("unsigned"), .width(3)) comparator_71 (
    .a(Instruction[14:12]), .b(3'b000), .eq(comparator_71_eq));  // open: gt, lt
  Comparator #(.mode("unsigned"), .width(7)) comparator_72 (
    .a(Instruction[6:0]), .b(7'b0000011), .eq(comparator_72_eq));  // open: gt, lt
  and and_44 (IsLh, comparator_72_eq, comparator_73_eq);
  Comparator #(.mode("unsigned"), .width(3)) comparator_73 (
    .a(Instruction[14:12]), .b(3'b001), .eq(comparator_73_eq));  // open: gt, lt
  Comparator #(.mode("unsigned"), .width(7)) comparator_74 (
    .a(Instruction[6:0]), .b(7'b0000011), .eq(comparator_74_eq));  // open: gt, lt
  and and_45 (IsLw, comparator_74_eq, comparator_75_eq);
  Comparator #(.mode("unsigned"), .width(3)) comparator_75 (
    .a(Instruction[14:12]), .b(3'b010), .eq(comparator_75_eq));  // open: gt, lt
  Comparator #(.mode("unsigned"), .width(7)) comparator_76 (
    .a(Instruction[6:0]), .b(7'b0100011), .eq(comparator_76_eq));  // open: gt, lt
  and and_46 (IsSb, comparator_76_eq, comparator_77_eq);
  Comparator #(.mode("unsigned"), .width(3)) comparator_77 (
    .a(Instruction[14:12]), .b(3'b000), .eq(comparator_77_eq));  // open: gt, lt
  Comparator #(.mode("unsigned"), .width(7)) comparator_78 (
    .a(Instruction[6:0]), .b(7'b0100011), .eq(comparator_78_eq));  // open: gt, lt
  and and_47 (IsSh, comparator_78_eq, comparator_79_eq);
  Comparator #(.mode("unsigned"), .width(3)) comparator_79 (
    .a(Instruction[14:12]), .b(3'b001), .eq(comparator_79_eq));  // open: gt, lt
  Comparator #(.mode("unsigned"), .width(7)) comparator_80 (
    .a(Instruction[6:0]), .b(7'b0100011), .eq(comparator_80_eq));  // open: gt, lt
  and and_48 (IsSw, comparator_80_eq, comparator_81_eq);
  Comparator #(.mode("unsigned"), .width(3)) comparator_81 (
    .a(Instruction[14:12]), .b(3'b010), .eq(comparator_81_eq));  // open: gt, lt
  // Probe on ROMIn
  Priority_Encoder #(.select_enc(6)) priority_encoder_1 (
    .in0(IsAdd), .in1(IsMul), .in2(IsSub), .in3(IsSll), .in4(IsMulh), .in5(IsMulhu), .in6(IsSlt),
    .in7(IsXor), .in8(IsSrl), .in9(IsSra), .in10(IsOr), .in11(IsAnd), .in12(IsLb), .in13(IsLh), .in14(IsLw),
    .in15(IsAddi), .in16(IsSlli), .in17(IsSlti), .in18(IsXori), .in19(IsSrli), .in20(IsSrai), .in21(IsOri),
    .in22(IsAndi), .in23(IsSb), .in24(IsSh), .in25(IsSw), .in26(IsBeq), .in27(IsBne), .in28(IsBlt),
    .in29(IsBge), .in30(IsBltu), .in31(IsBgeu), .in32(IsAuipc), .in33(IsLui), .in34(IsJal), .in35(IsJalr),
    .in36(undriven), .in37(undriven_2), .in38(undriven_3), .in39(undriven_4), .in40(undriven_5),
    .in41(undriven_6), .in42(undriven_7), .in43(undriven_8), .in44(undriven_9), .in45(undriven_10),
    .in46(undriven_11), .in47(undriven_12), .in48(undriven_13), .in49(undriven_14), .in50(undriven_15),
    .in51(undriven_16), .in52(undriven_17), .in53(undriven_18), .in54(undriven_19), .in55(undriven_20),
    .in56(undriven_21), .in57(undriven_22), .in58(undriven_23), .in59(undriven_24), .in60(undriven_25),
    .in61(undriven_26), .in62(undriven_27), .in63(undriven_28), .out(ROMIn));  // open: gs, en_out, en_in
  Comparator #(.mode("unsigned"), .width(7)) comparator_82 (
    .a(Instruction[6:0]), .b(7'b1101111), .eq(IsJal));  // open: gt, lt
  Comparator #(.mode("unsigned"), .width(7)) comparator_83 (
    .a(Instruction[6:0]), .b(7'b1100111), .eq(comparator_83_eq));  // open: gt, lt
  Comparator #(.mode("unsigned"), .width(3)) comparator_84 (
    .a(Instruction[14:12]), .b(3'b000), .eq(comparator_84_eq));  // open: gt, lt
  Comparator #(.mode("unsigned"), .width(7)) comparator_85 (
    .a(Instruction[6:0]), .b(7'b0010111), .eq(IsAuipc));  // open: gt, lt
  Comparator #(.mode("unsigned"), .width(7)) comparator_86 (
    .a(Instruction[6:0]), .b(7'b0110111), .eq(IsLui));  // open: gt, lt
  and and_49 (and_49_out, IsBeq, BrEq);
  or or_1 (or_1_out, IsBgeu, IsBge);
  or or_2 (or_2_out, IsBlt, IsBltu);
  and and_50 (and_50_out, IsBne, ~BrEq);  // AND_Gate
  or or_3 (or_3_out, IsJal, IsJalr);
  and and_51 (IsJalr, comparator_83_eq, comparator_84_eq);
  and and_52 (and_52_out, or_1_out, ~BrLt);  // AND_Gate
  and and_53 (and_53_out, or_2_out, BrLt);
  or or_4 (PCSel, or_5_out, or_3_out);
  or or_5 (or_5_out, and_49_out, and_52_out, and_53_out, and_50_out);

  // Other names for the same wires on the sheet: Opcode[6:0] = Instruction[6:0]; RdImm[4:0] = Instruction[11:7];
  //   funct3[2:0] = Instruction[14:12]; Imm12[19:0] = Instruction[31:12]; Rs1[4:0] = Instruction[19:15];
  //   Imm20[11:0] = Instruction[31:20]; Rs2Imm[4:0] = Instruction[24:20]; Funct7Imm[6:0] = Instruction[31:25]

  // Notes on the sheet:
  //   INPUTS to your circuit
  //   Connect ROM Input here ->
  //   contents of rom_1 (hex, n*v repeats v):
  //   1001 1401 1601 1081 1481 1581 1101 1201 1281 1681 1301 1381 41 41 41 1041 10c1 1141 1241 12c1 16c1
  //   1341 13c1 842 842 842 4*64 74 74 1067 17c7 2069 2041
  //   ROM FOR CONTROL LOGIC
  //   DON'T CHANGE THE LOCATIONS OF THE INPUTS AND OUTPUTS!
  //   This is only if you choose to do the ROM option
  //   CONNECT
  //   WIRE
  //   TO
  //   USE
  //   ROM
  //   OUTPUT from your circuit
  //   Reminder: If using ROM, use combinational logic for PCSel
endmodule
