// Logisim project cpu.circ as structural Verilog: 1 circuit, main circuit cpu
module cpu (
  input  clk,
  input  [31:0] Instruction,
  input  [31:0] MemReadData,
  output [31:0] MemAddress,
  output [31:0] ProgramCounter,
  output [31:0] ra,
  output [31:0] sp,
  output [31:0] t0,
  output [31:0] t1,
  output [31:0] t2,
  output [31:0] s0,
  output [31:0] s1,
  output [31:0] a0,
  output [3:0] MemWriteMask,
  output [31:0] MemWriteData
);

  wire ASel, BrEq, BrLt, BrUn, BSel, MemWEn, PCSel, RegWEn;
  wire [1:0] WBSel;
  wire [2:0] funct3, ImmSel;
  wire [3:0] ALUSel;
  wire [31:0] Immediate, InstructionP, multiplexer_1_out, multiplexer_2_out, multiplexer_3_out,
       multiplexer_4_out, partial_load_1_datatoreg, PC4, PC4P, ProgramCounterP, ReadData1, ReadData2,
       RegWData;

  // Probe on MemAddress
  Adder #(.width(32)) adder_1 (.a(ProgramCounter), .b(32'h4), .out(PC4));  // open: cin, cout
  // Probe on multiplexer_1_out
  Register #(.width(32)) PC (.D(multiplexer_1_out), .clk(clk), .Q(ProgramCounter));  // open: en, clr
  Multiplexer #(.width(32)) multiplexer_1 (.in0(PC4), .in1(MemAddress), .out(multiplexer_1_out), .sel(PCSel));
  Multiplexer #(.width(32)) multiplexer_2 (.in0(Instruction), .in1(32'h13), .out(multiplexer_2_out), .sel(PCSel));
  Register #(.width(32)) PipelinePC4 (.D(PC4), .clk(clk), .Q(PC4P));  // open: en, clr
  Register #(.width(32)) PipelinePC (.D(ProgramCounter), .clk(clk), .Q(ProgramCounterP));  // open: en, clr
  Register #(.width(32)) PipelineImm (
    .D(multiplexer_2_out), .clk(clk), .Q({InstructionP[31:15], funct3, InstructionP[11:0]}));  // open: en, clr
  // Probe on ra
  control_logic control_logic_1 (
    .Instruction({InstructionP[31:15], funct3, InstructionP[11:0]}), .BrEq(BrEq), .BrLt(BrLt), .PCSel(PCSel),
    .RegWEn(RegWEn), .ImmSel(ImmSel), .BrUn(BrUn), .ASel(ASel), .BSel(BSel), .ALUSel(ALUSel),
    .MemWEn(MemWEn), .WBSel(WBSel));
  regfile regfile_1 (
    .ReadIndex1(InstructionP[19:15]), .ReadIndex2(InstructionP[24:20]), .WriteIndex(InstructionP[11:7]),
    .WriteData(RegWData), .RegWEn(RegWEn), .clk(clk), .ra(ra), .sp(sp), .t0(t0), .t1(t1), .t2(t2), .s0(s0),
    .s1(s1), .a0(a0), .ReadData1(ReadData1), .ReadData2(ReadData2));
  // Probe on Immediate
  imm_gen imm_gen_1 (
    .Instruction({InstructionP[31:15], funct3, InstructionP[11:0]}), .ImmSel(ImmSel), .Immediate(Immediate));
  // Probe on ReadData1
  // Probe on ReadData2
  // Probe on ProgramCounterP
  // Probe on multiplexer_3_out
  Multiplexer #(.width(32)) multiplexer_3 (.in0(ReadData1), .in1(ProgramCounterP), .out(multiplexer_3_out), .sel(ASel));
  // Probe on multiplexer_4_out
  Multiplexer #(.width(32)) multiplexer_4 (.in0(ReadData2), .in1(Immediate), .out(multiplexer_4_out), .sel(BSel));
  branch_comp branch_comp_1 (.BrData1(ReadData1), .BrData2(ReadData2), .BrUn(BrUn), .BrEq(BrEq), .BrLt(BrLt));
  alu alu_1 (.A(multiplexer_3_out), .B(multiplexer_4_out), .ALUSel(ALUSel), .ALUResult(MemAddress));
  // Probe on ALUSel
  // Probe on MemAddress
  partial_store partial_store_1 (
    .Instruction({InstructionP[31:15], funct3, InstructionP[11:0]}), .MemAddress(MemAddress),
    .DataFromReg(ReadData2), .MemWEn(MemWEn), .MemWriteMask(MemWriteMask), .DataToMem(MemWriteData));
  partial_load partial_load_1 (
    .Instruction({InstructionP[31:15], funct3, InstructionP[11:0]}), .MemAddress(MemAddress),
    .DataFromMem(MemReadData), .DataToReg(partial_load_1_datatoreg));
  // Probe on RegWData
  Multiplexer #(.select(2), .width(32)) multiplexer_5 (
    .in0(partial_load_1_datatoreg), .in1(MemAddress), .in2(PC4P), .out(RegWData), .sel(WBSel));  // open: in3

  // Other names for the same wires on the sheet: ALUResult[31:0] = MemAddress; opcode[6:0] = InstructionP[6:0];
  //   rd[4:0] = InstructionP[11:7]; InstructionP[14:12] = funct3; rs1[4:0] = InstructionP[19:15];
  //   rs2[4:0] = InstructionP[24:20]

  // Notes on the sheet:
  //   To IMEM
  //   IMEM (do **NOT** move this)
  //   From IMEM
  //   Inputs/Outputs for testing. Do **NOT** move these.
  //   To DMEM
  //   DMEM (do **NOT** move this)
  //   From DMEM
endmodule
