// Logisim project partial-store.circ as structural Verilog: 1 circuit, main circuit partial_store
module partial_store (
  input  [31:0] Instruction,
  input  [31:0] MemAddress,
  input  [31:0] DataFromReg,
  input  MemWEn,
  output [3:0] MemWriteMask,
  output [31:0] DataToMem
);

  wire comparator_1_eq, comparator_2_eq, comparator_3_eq, comparator_4_eq, comparator_5_eq, comparator_6_eq,
       IsSb, IsSh, IsSw;
  wire [1:0] SSel;
  wire [3:0] multiplexer_1_out, multiplexer_2_out, multiplexer_5_out;
  wire [15:0] undriven_6;
  wire [23:0] undriven_4;
  wire [31:0] multiplexer_3_out, multiplexer_4_out, undriven_2, undriven_3;
  wire [31:8] undriven;
  wire [31:16] undriven_5;

  Comparator #(.width(7)) comparator_1 (.a(Instruction[6:0]), .b(7'b0100011), .eq(comparator_1_eq));  // open: gt, lt
  Comparator #(.width(3)) comparator_2 (.a(Instruction[14:12]), .b(3'b000), .eq(comparator_2_eq));  // open: gt, lt
  Comparator #(.width(7)) comparator_3 (.a(Instruction[6:0]), .b(7'b0100011), .eq(comparator_3_eq));  // open: gt, lt
  Comparator #(.width(3)) comparator_4 (.a(Instruction[14:12]), .b(3'b001), .eq(comparator_4_eq));  // open: gt, lt
  Comparator #(.width(7)) comparator_5 (.a(Instruction[6:0]), .b(7'b0100011), .eq(comparator_5_eq));  // open: gt, lt
  Comparator #(.width(3)) comparator_6 (.a(Instruction[14:12]), .b(3'b010), .eq(comparator_6_eq));  // open: gt, lt
  and and_1 (IsSb, comparator_1_eq, comparator_2_eq);
  and and_2 (IsSh, comparator_3_eq, comparator_4_eq);
  and and_3 (IsSw, comparator_5_eq, comparator_6_eq);
  Priority_Encoder #(.select_enc(2)) priority_encoder_1 (
    .in0(1'b1), .in1(IsSb), .in2(IsSh), .in3(IsSw), .out(SSel));  // open: gs, en_out, en_in
  Multiplexer #(.select(2), .width(4)) multiplexer_1 (
    .in0(4'b0001), .in1(4'b0010), .in2(4'b0100), .in3(4'b1000), .out(multiplexer_1_out), .sel(MemAddress[1:0]));
  Multiplexer #(.select(2), .width(4)) multiplexer_2 (
    .in0(4'b0011), .in2(4'b1100), .out(multiplexer_2_out), .sel(MemAddress[1:0]));  // open: in1, in3
  Multiplexer #(.select(2), .width(32)) multiplexer_3 (
    .in0({undriven, DataFromReg[7:0]}), .in1({undriven_2[31:16], DataFromReg[7:0], undriven_2[7:0]}),
    .in2({undriven_3[31:24], DataFromReg[7:0], undriven_3[15:0]}), .in3({DataFromReg[7:0], undriven_4}),
    .out(multiplexer_3_out), .sel(MemAddress[1:0]));
  Multiplexer #(.select(2), .width(32)) multiplexer_4 (
    .in0({undriven_5, DataFromReg[15:0]}), .in2({DataFromReg[15:0], undriven_6}), .out(multiplexer_4_out),
    .sel(MemAddress[1:0]));  // open: in1, in3
  Multiplexer #(.select(2), .width(4)) multiplexer_5 (
    .in0(4'b0000), .in1(multiplexer_1_out), .in2(multiplexer_2_out), .in3(4'b1111), .out(multiplexer_5_out),
    .sel(SSel));
  // Probe on MemWriteMask
  Multiplexer #(.width(4)) multiplexer_6 (.in0(4'b0000), .in1(multiplexer_5_out), .out(MemWriteMask), .sel(MemWEn));
  Multiplexer #(.select(3), .width(32)) multiplexer_7 (
    .in0(multiplexer_3_out), .in1(multiplexer_4_out), .in2(DataFromReg), .out(DataToMem),
    .sel(Instruction[14:12]));  // open: in3, in4, in5, in6, in7

  // Other names for the same wires on the sheet: Opcode[6:0] = Instruction[6:0]; Funct3[2:0] = Instruction[14:12];
  //   Bottom2[1:0] = MemAddress[1:0]

  // Notes on the sheet:
  //   INPUTS to your circuit
  //   DON'T CHANGE THE LOCATIONS OF THE INPUTS AND OUTPUTS!
  //   OUTPUT from your circuit
endmodule
