// Logisim project regfile.circ as structural Verilog: 1 circuit, main circuit regfile
module regfile (
  input  [4:0] ReadIndex1,
  input  [4:0] ReadIndex2,
  input  [4:0] WriteIndex,
  input  [31:0] WriteData,
  input  RegWEn,
  input  clk,
  output [31:0] ra,
  output [31:0] sp,
  output [31:0] t0,
  output [31:0] t1,
  output [31:0] t2,
  output [31:0] s0,
  output [31:0] s1,
  output [31:0] a0,
  output [31:0] ReadData1,
  output [31:0] ReadData2
);

  wire x1WEn, x2WEn, x3WEn, x4WEn, x5WEn, x6WEn, x7WEn, x8WEn, x9WEn, x10WEn, x11WEn, x12WEn, x13WEn, x14WEn,
       x15WEn, x16WEn, x17WEn, x18WEn, x19WEn, x20WEn, x21WEn, x22WEn, x23WEn, x24WEn, x25WEn, x26WEn,
       x27WEn, x28WEn, x29WEn, x30WEn, x31WEn;
  wire [31:0] x0, x3, x4, x11, x12, x13, x14, x15, x16, x17, x18, x19, x20, x21, x22, x23, x24, x25, x26,
       x27, x28, x29, x30, x31;

  Register #(.width(32)) register_1 (.D({32{1'b0}}), .en(1'b0), .clk(clk), .Q(x0));  // open: clr
  Register #(.width(32)) register_2 (.D(WriteData), .en(x4WEn), .clk(clk), .Q(x4));  // open: clr
  Register #(.width(32)) register_3 (.D(WriteData), .en(x8WEn), .clk(clk), .Q(s0));  // open: clr
  Register #(.width(32)) register_4 (.D(WriteData), .en(x12WEn), .clk(clk), .Q(x12));  // open: clr
  Register #(.width(32)) register_5 (.D(WriteData), .en(x16WEn), .clk(clk), .Q(x16));  // open: clr
  Register #(.width(32)) register_6 (.D(WriteData), .en(x20WEn), .clk(clk), .Q(x20));  // open: clr
  Register #(.width(32)) register_7 (.D(WriteData), .en(x24WEn), .clk(clk), .Q(x24));  // open: clr
  Register #(.width(32)) register_8 (.D(WriteData), .en(x28WEn), .clk(clk), .Q(x28));  // open: clr
  Multiplexer #(.select(5), .width(32)) multiplexer_1 (
    .in0(x0), .in1(ra), .in2(sp), .in3(x3), .in4(x4), .in5(t0), .in6(t1), .in7(t2), .in8(s0), .in9(s1),
    .in10(a0), .in11(x11), .in12(x12), .in13(x13), .in14(x14), .in15(x15), .in16(x16), .in17(x17),
    .in18(x18), .in19(x19), .in20(x20), .in21(x21), .in22(x22), .in23(x23), .in24(x24), .in25(x25),
    .in26(x26), .in27(x27), .in28(x28), .in29(x29), .in30(x30), .in31(x31), .out(ReadData1), .sel(ReadIndex1));
  Register #(.width(32)) register_9 (.D(WriteData), .en(x1WEn), .clk(clk), .Q(ra));  // open: clr
  Register #(.width(32)) register_10 (.D(WriteData), .en(x5WEn), .clk(clk), .Q(t0));  // open: clr
  Register #(.width(32)) register_11 (.D(WriteData), .en(x9WEn), .clk(clk), .Q(s1));  // open: clr
  Register #(.width(32)) register_12 (.D(WriteData), .en(x13WEn), .clk(clk), .Q(x13));  // open: clr
  Register #(.width(32)) register_13 (.D(WriteData), .en(x17WEn), .clk(clk), .Q(x17));  // open: clr
  Register #(.width(32)) register_14 (.D(WriteData), .en(x21WEn), .clk(clk), .Q(x21));  // open: clr
  Register #(.width(32)) register_15 (.D(WriteData), .en(x25WEn), .clk(clk), .Q(x25));  // open: clr
  Register #(.width(32)) register_16 (.D(WriteData), .en(x29WEn), .clk(clk), .Q(x29));  // open: clr
  Register #(.width(32)) register_17 (.D(WriteData), .en(x2WEn), .clk(clk), .Q(sp));  // open: clr
  Register #(.width(32)) register_18 (.D(WriteData), .en(x6WEn), .clk(clk), .Q(t1));  // open: clr
  Register #(.width(32)) register_19 (.D(WriteData), .en(x10WEn), .clk(clk), .Q(a0));  // open: clr
  Register #(.width(32)) register_20 (.D(WriteData), .en(x14WEn), .clk(clk), .Q(x14));  // open: clr
  Register #(.width(32)) register_21 (.D(WriteData), .en(x18WEn), .clk(clk), .Q(x18));  // open: clr
  Register #(.width(32)) register_22 (.D(WriteData), .en(x22WEn), .clk(clk), .Q(x22));  // open: clr
  Register #(.width(32)) register_23 (.D(WriteData), .en(x26WEn), .clk(clk), .Q(x26));  // open: clr
  Register #(.width(32)) register_24 (.D(WriteData), .en(x30WEn), .clk(clk), .Q(x30));  // open: clr
  Multiplexer #(.select(5), .width(32)) multiplexer_2 (
    .in0(x0), .in1(ra), .in2(sp), .in3(x3), .in4(x4), .in5(t0), .in6(t1), .in7(t2), .in8(s0), .in9(s1),
    .in10(a0), .in11(x11), .in12(x12), .in13(x13), .in14(x14), .in15(x15), .in16(x16), .in17(x17),
    .in18(x18), .in19(x19), .in20(x20), .in21(x21), .in22(x22), .in23(x23), .in24(x24), .in25(x25),
    .in26(x26), .in27(x27), .in28(x28), .in29(x29), .in30(x30), .in31(x31), .out(ReadData2), .sel(ReadIndex2));
  Register #(.width(32)) register_25 (.D(WriteData), .en(x3WEn), .clk(clk), .Q(x3));  // open: clr
  Register #(.width(32)) register_26 (.D(WriteData), .en(x7WEn), .clk(clk), .Q(t2));  // open: clr
  Register #(.width(32)) register_27 (.D(WriteData), .en(x11WEn), .clk(clk), .Q(x11));  // open: clr
  Register #(.width(32)) register_28 (.D(WriteData), .en(x15WEn), .clk(clk), .Q(x15));  // open: clr
  Register #(.width(32)) register_29 (.D(WriteData), .en(x19WEn), .clk(clk), .Q(x19));  // open: clr
  Register #(.width(32)) register_30 (.D(WriteData), .en(x23WEn), .clk(clk), .Q(x23));  // open: clr
  Register #(.width(32)) register_31 (.D(WriteData), .en(x27WEn), .clk(clk), .Q(x27));  // open: clr
  Register #(.width(32)) register_32 (.D(WriteData), .en(x31WEn), .clk(clk), .Q(x31));  // open: clr
  Demultiplexer #(.select(5)) demultiplexer_1 (
    .out1(x1WEn), .out2(x2WEn), .out3(x3WEn), .out4(x4WEn), .out5(x5WEn), .out6(x6WEn), .out7(x7WEn),
    .out8(x8WEn), .out9(x9WEn), .out10(x10WEn), .out11(x11WEn), .out12(x12WEn), .out13(x13WEn),
    .out14(x14WEn), .out15(x15WEn), .out16(x16WEn), .out17(x17WEn), .out18(x18WEn), .out19(x19WEn),
    .out20(x20WEn), .out21(x21WEn), .out22(x22WEn), .out23(x23WEn), .out24(x24WEn), .out25(x25WEn),
    .out26(x26WEn), .out27(x27WEn), .out28(x28WEn), .out29(x29WEn), .out30(x30WEn), .out31(x31WEn),
    .in(RegWEn), .sel(WriteIndex));  // open: out0

  // Other names for the same wires on the sheet: x1[31:0] = ra; x2[31:0] = sp; x5[31:0] = t0; x6[31:0] = t1;
  //   x7[31:0] = t2; x8[31:0] = s0; x9[31:0] = s1; x10[31:0] = a0

  // Notes on the sheet:
  //   INPUTS to your circuit
  //   DON'T CHANGE THE LOCATIONS OF THE INPUTS AND OUTPUTS!
  //   These are DEBUG/TEST outputs from your circuit.
  //   OUTPUTS from your circuit
endmodule
